// Logisim project relogioversaofinal.circ as structural Verilog
module relogio (
);

  wire and_1_out, and_2_out, and_3_out, and_4_out, and_5_out, and_6_out, and_7_out, and_8_out, and_9_out,
       CLEAR_TOTAL_out, clock_1_out;
  wire [3:0] cont05_1_out_5, cont05_2_out_5, cont05_3_out_5, cont09_1_out_5, cont09_2_out_5, cont09_3_out_5;

  and and_1 (and_1_out, ~cont09_1_out_5[0], ~cont09_1_out_5[1], cont09_1_out_5[2], ~cont09_1_out_5[3]);  // AND_Gate
  and and_2 (and_2_out, ~cont05_1_out_5[0], cont05_1_out_5[1], ~cont05_1_out_5[2], ~cont05_1_out_5[3]);  // AND_Gate
  and and_3 (and_3_out, cont05_1_out_5[0], cont05_1_out_5[1], ~cont05_1_out_5[2], ~cont05_1_out_5[3]);  // AND_Gate
  and and_4 (and_4_out, and_1_out, and_2_out);
  Button CLEAR_TOTAL (.out(CLEAR_TOTAL_out));
  Hex_Digit_Display hex_digit_display_1 (.value(cont05_1_out_5));  // open: dp
  cont05 cont05_1 (
    .out_5(cont05_1_out_5), .clock(and_5_out), .clear(and_3_out), .clear2(CLEAR_TOTAL_out), .clear3(and_4_out));
  Hex_Digit_Display hex_digit_display_2 (.value(cont09_1_out_5));  // open: dp
  cont09 cont09_1 (
    .out_5(cont09_1_out_5), .clock(and_6_out), .clear(and_5_out), .clear2(and_4_out), .clear3(CLEAR_TOTAL_out));
  and and_5 (and_5_out, ~cont09_1_out_5[0], cont09_1_out_5[1], ~cont09_1_out_5[2], cont09_1_out_5[3]);  // AND_Gate
  Hex_Digit_Display hex_digit_display_3 (.value(cont05_2_out_5));  // open: dp
  cont05 cont05_2 (
    .out_5(cont05_2_out_5), .clock(and_7_out), .clear(and_6_out), .clear2(CLEAR_TOTAL_out));  // open: clear3
  Hex_Digit_Display hex_digit_display_4 (.value(cont09_2_out_5));  // open: dp
  cont09 cont09_2 (
    .out_5(cont09_2_out_5), .clock(and_8_out), .clear(and_7_out), .clear3(CLEAR_TOTAL_out));  // open: clear2
  and and_6 (and_6_out, ~cont05_2_out_5[0], cont05_2_out_5[1], cont05_2_out_5[2], ~cont05_2_out_5[3]);  // AND_Gate
  and and_7 (and_7_out, ~cont09_2_out_5[0], cont09_2_out_5[1], ~cont09_2_out_5[2], cont09_2_out_5[3]);  // AND_Gate
  Hex_Digit_Display hex_digit_display_5 (.value(cont09_3_out_5));  // open: dp
  Hex_Digit_Display hex_digit_display_6 (.value(cont05_3_out_5));  // open: dp
  cont09 cont09_3 (
    .out_5(cont09_3_out_5), .clock(clock_1_out), .clear(and_9_out), .clear3(CLEAR_TOTAL_out));  // open: clear2
  cont05 cont05_3 (
    .out_5(cont05_3_out_5), .clock(and_9_out), .clear(and_8_out), .clear2(CLEAR_TOTAL_out));  // open: clear3
  and and_8 (and_8_out, ~cont05_3_out_5[0], cont05_3_out_5[1], cont05_3_out_5[2], ~cont05_3_out_5[3]);  // AND_Gate
  and and_9 (and_9_out, ~cont09_3_out_5[0], cont09_3_out_5[1], ~cont09_3_out_5[2], cont09_3_out_5[3]);  // AND_Gate
  Clock clock_1 (.out(clock_1_out));

  // Notes on the sheet:
  //   RELÓGIO DIGITAL
  //   MATHEUS FIOD SALIBA
  //   CAIKE CESAR MOTA DE ARAÚJO
  //   AMANDA DUARTE DE GARCIA
  //   (12221BCC024)
  //   (12221BCC030)
  //   (12221BCC031)
endmodule

module cont09 (
  input  clock,
  input  clear,
  input  clear2,
  input  clear3,
  output [3:0] out_5
);

  wire or_1_out, or_2_out, or_3_out, or_4_out;

  or or_1 (or_1_out, clear, clear3, clear2);
  T_Flip_Flop #(.trigger("falling")) t_ff_1 (
    .clk(clock), .T(1'b1), .Q(out_5[0]), .reset(or_1_out));  // open: Qn, preset, en
  T_Flip_Flop #(.trigger("falling")) t_ff_2 (
    .clk(out_5[0]), .T(1'b1), .Q(out_5[1]), .reset(or_2_out));  // open: Qn, preset, en
  or or_2 (or_2_out, clear, clear3, clear2);
  T_Flip_Flop #(.trigger("falling")) t_ff_3 (
    .clk(out_5[1]), .T(1'b1), .Q(out_5[2]), .reset(or_3_out));  // open: Qn, preset, en
  or or_3 (or_3_out, clear, clear3, clear2);
  T_Flip_Flop #(.trigger("falling")) t_ff_4 (
    .clk(out_5[2]), .T(1'b1), .Q(out_5[3]), .reset(or_4_out));  // open: Qn, preset, en
  or or_4 (or_4_out, clear, clear3, clear2);
endmodule

module cont05 (
  input  clock,
  input  clear2,
  input  clear,
  input  clear3,
  output [3:0] out_5
);

  wire or_1_out, or_2_out, or_3_out;

  T_Flip_Flop #(.trigger("falling")) t_ff_1 (
    .clk(clock), .T(1'b1), .Q(out_5[0]), .reset(or_1_out));  // open: Qn, preset, en
  or or_1 (or_1_out, clear, clear3, clear2);
  T_Flip_Flop #(.trigger("falling")) t_ff_2 (
    .clk(out_5[0]), .T(1'b1), .Q(out_5[1]), .reset(or_2_out));  // open: Qn, preset, en
  or or_2 (or_2_out, clear, clear3, clear2);
  T_Flip_Flop #(.trigger("falling")) t_ff_3 (
    .clk(out_5[1]), .T(1'b1), .Q(out_5[2]), .reset(or_3_out));  // open: Qn, preset, en
  or or_3 (or_3_out, clear, clear3, clear2);

  assign out_5[3] = 1'b0;
endmodule
